// Digital circuit Carry_LA.dig as structural Verilog
module Carry_LA (
  input  c0,
  input  b0,
  input  a0,
  input  b1,
  input  a1,
  input  b2,
  input  a2,
  input  b3,
  input  a3,
  output S0,
  output S1,
  output S3,
  output S2,
  output C4
);

  wire and_1_out, and_2_out, and_3_out, and_4_out, and_5_out, and_6_out, and_7_out, and_8_out, and_9_out,
       and_10_out, or_1_out, or_2_out, or_3_out, somador_g_p_1_g, somador_g_p_1_p, somador_g_p_2_g,
       somador_g_p_2_p, somador_g_p_3_g, somador_g_p_3_p, somador_g_p_4_g, somador_g_p_4_p;

  Somador_G_P somador_g_p_1 (.B(b0), .A(a0), .G(somador_g_p_1_g), .P(somador_g_p_1_p));
  xor xor_1 (S0, c0, somador_g_p_1_g);
  Somador_G_P somador_g_p_2 (.B(b1), .A(a1), .G(somador_g_p_2_g), .P(somador_g_p_2_p));
  and and_1 (and_1_out, c0, somador_g_p_1_g);
  or or_1 (or_1_out, somador_g_p_1_p, and_1_out);
  xor xor_2 (S1, or_1_out, somador_g_p_2_g);
  Somador_G_P somador_g_p_3 (.B(b2), .A(a2), .G(somador_g_p_3_g), .P(somador_g_p_3_p));
  and and_2 (and_2_out, somador_g_p_1_p, somador_g_p_2_g);
  and and_3 (and_3_out, c0, somador_g_p_1_g, somador_g_p_2_g);
  or or_2 (or_2_out, and_3_out, and_2_out, somador_g_p_2_p);
  xor xor_3 (S2, or_2_out, somador_g_p_3_g);
  Somador_G_P somador_g_p_4 (.B(b3), .A(a3), .G(somador_g_p_4_g), .P(somador_g_p_4_p));
  and and_4 (and_4_out, c0, somador_g_p_1_g, somador_g_p_2_g, somador_g_p_3_g);
  and and_5 (and_5_out, somador_g_p_1_p, somador_g_p_2_g, somador_g_p_3_g);
  and and_6 (and_6_out, somador_g_p_2_p, somador_g_p_3_g);
  and and_7 (and_7_out, somador_g_p_1_p, somador_g_p_1_g, somador_g_p_2_g, somador_g_p_3_g, somador_g_p_4_g);
  and and_8 (and_8_out, somador_g_p_1_p, somador_g_p_2_g, somador_g_p_3_g, somador_g_p_4_g);
  and and_9 (and_9_out, somador_g_p_2_p, somador_g_p_3_g, somador_g_p_4_g);
  and and_10 (and_10_out, somador_g_p_3_p, somador_g_p_4_g);
  or or_3 (or_3_out, and_4_out, and_5_out, and_6_out);
  or or_4 (C4, and_7_out, and_8_out, and_9_out, and_10_out, somador_g_p_4_p);
  xor xor_4 (S3, or_3_out, somador_g_p_4_g);
endmodule
