// Digital circuit IP + 1.dig as structural Verilog
module IP___1 (
  input  [23:0] D,
  input  clk,
  output [23:0] Q
);

  _1_bit_FF _1_bit_ff_1 (.D(D[0]), .clk(clk), .Q(Q[0]));
  _1_bit_FF _1_bit_ff_2 (.D(D[1]), .clk(clk), .Q(Q[1]));
  _1_bit_FF _1_bit_ff_3 (.D(D[2]), .clk(clk), .Q(Q[2]));
  _1_bit_FF _1_bit_ff_4 (.D(D[3]), .clk(clk), .Q(Q[3]));
  _1_bit_FF _1_bit_ff_5 (.D(D[4]), .clk(clk), .Q(Q[4]));
  _1_bit_FF _1_bit_ff_6 (.D(D[5]), .clk(clk), .Q(Q[5]));
  _1_bit_FF _1_bit_ff_7 (.D(D[6]), .clk(clk), .Q(Q[6]));
  _1_bit_FF _1_bit_ff_8 (.D(D[7]), .clk(clk), .Q(Q[7]));
  _1_bit_FF _1_bit_ff_9 (.D(D[8]), .clk(clk), .Q(Q[8]));
  _1_bit_FF _1_bit_ff_10 (.D(D[9]), .clk(clk), .Q(Q[9]));
  _1_bit_FF _1_bit_ff_11 (.D(D[10]), .clk(clk), .Q(Q[10]));
  _1_bit_FF _1_bit_ff_12 (.D(D[11]), .clk(clk), .Q(Q[11]));
  _1_bit_FF _1_bit_ff_13 (.D(D[12]), .clk(clk), .Q(Q[12]));
  _1_bit_FF _1_bit_ff_14 (.D(D[13]), .clk(clk), .Q(Q[13]));
  _1_bit_FF _1_bit_ff_15 (.D(D[14]), .clk(clk), .Q(Q[14]));
  _1_bit_FF _1_bit_ff_16 (.D(D[15]), .clk(clk), .Q(Q[15]));
  _1_bit_FF _1_bit_ff_17 (.D(D[16]), .clk(clk), .Q(Q[16]));
  _1_bit_FF _1_bit_ff_18 (.D(D[17]), .clk(clk), .Q(Q[17]));
  _1_bit_FF _1_bit_ff_19 (.D(D[18]), .clk(clk), .Q(Q[18]));
  _1_bit_FF _1_bit_ff_20 (.D(D[19]), .clk(clk), .Q(Q[19]));
  _1_bit_FF _1_bit_ff_21 (.D(D[20]), .clk(clk), .Q(Q[20]));
  _1_bit_FF _1_bit_ff_22 (.D(D[21]), .clk(clk), .Q(Q[21]));
  _1_bit_FF _1_bit_ff_23 (.D(D[22]), .clk(clk), .Q(Q[22]));
  _1_bit_FF _1_bit_ff_24 (.D(D[23]), .clk(clk), .Q(Q[23]));
endmodule
