// Digital circuit Registrador32bit.dig as structural Verilog
module Registrador32bit (
  input  [31:0] C,
  input  [3:0] a_2,
  input  [3:0] b_2,
  input  [3:0] c_2,
  input  EN,
  input  clk,
  output [31:0] A,
  output [31:0] B
);

  wire and_1_out, demultiplexer_1_out_0, demultiplexer_1_out_1, demultiplexer_1_out_2, demultiplexer_1_out_3,
       demultiplexer_1_out_4, demultiplexer_1_out_5, demultiplexer_1_out_6, demultiplexer_1_out_7,
       demultiplexer_1_out_8, demultiplexer_1_out_9, demultiplexer_1_out_10, demultiplexer_1_out_11,
       demultiplexer_1_out_12, demultiplexer_1_out_13, demultiplexer_1_out_14, demultiplexer_1_out_15;
  wire [31:0] _0, _1, _2, _3, _4, _5, _6, _7, _8, _9, _10, _11, _12, _13, _14, _15;

  and and_1 (and_1_out, EN, clk);
  Demultiplexer #(.Selector_Bits(4)) demultiplexer_1 (
    .sel(c_2), .in(and_1_out), .out_0(demultiplexer_1_out_0), .out_1(demultiplexer_1_out_1),
    .out_2(demultiplexer_1_out_2), .out_3(demultiplexer_1_out_3), .out_4(demultiplexer_1_out_4),
    .out_5(demultiplexer_1_out_5), .out_6(demultiplexer_1_out_6), .out_7(demultiplexer_1_out_7),
    .out_8(demultiplexer_1_out_8), .out_9(demultiplexer_1_out_9), .out_10(demultiplexer_1_out_10),
    .out_11(demultiplexer_1_out_11), .out_12(demultiplexer_1_out_12), .out_13(demultiplexer_1_out_13),
    .out_14(demultiplexer_1_out_14), .out_15(demultiplexer_1_out_15));
  Flipflop flipflop_1 (.D({32{1'b0}}), .clk(demultiplexer_1_out_0), .Q(_0));
  Flipflop flipflop_2 (.D(C), .clk(demultiplexer_1_out_1), .Q(_1));
  Flipflop flipflop_3 (.D(C), .clk(demultiplexer_1_out_2), .Q(_2));
  Flipflop flipflop_4 (.D(C), .clk(demultiplexer_1_out_3), .Q(_3));
  Flipflop flipflop_5 (.D(C), .clk(demultiplexer_1_out_4), .Q(_4));
  Flipflop flipflop_6 (.D(C), .clk(demultiplexer_1_out_5), .Q(_5));
  Flipflop flipflop_7 (.D(C), .clk(demultiplexer_1_out_6), .Q(_6));
  Flipflop flipflop_8 (.D(C), .clk(demultiplexer_1_out_7), .Q(_7));
  Flipflop flipflop_9 (.D(C), .clk(demultiplexer_1_out_8), .Q(_8));
  Flipflop flipflop_10 (.D(C), .clk(demultiplexer_1_out_9), .Q(_9));
  Flipflop flipflop_11 (.D(C), .clk(demultiplexer_1_out_10), .Q(_10));
  Flipflop flipflop_12 (.D(C), .clk(demultiplexer_1_out_11), .Q(_11));
  Flipflop flipflop_13 (.D(C), .clk(demultiplexer_1_out_12), .Q(_12));
  Flipflop flipflop_14 (.D(C), .clk(demultiplexer_1_out_13), .Q(_13));
  Flipflop flipflop_15 (.D(C), .clk(demultiplexer_1_out_14), .Q(_14));
  Flipflop flipflop_16 (.D(C), .clk(demultiplexer_1_out_15), .Q(_15));
  Multiplexer #(.Selector_Bits(4), .Bits(32)) multiplexer_1 (
    .sel(a_2), .in_0(_0), .in_1(_1), .in_2(_2), .in_3(_3), .in_4(_4), .in_5(_5), .in_6(_6), .in_7(_7),
    .in_8(_8), .in_9(_9), .in_10(_10), .in_11(_11), .in_12(_12), .in_13(_13), .in_14(_14), .in_15(_15),
    .out(A));
  Multiplexer #(.Selector_Bits(4), .Bits(32)) multiplexer_2 (
    .sel(b_2), .in_0(_0), .in_1(_1), .in_2(_2), .in_3(_3), .in_4(_4), .in_5(_5), .in_6(_6), .in_7(_7),
    .in_8(_8), .in_9(_9), .in_10(_10), .in_11(_11), .in_12(_12), .in_13(_13), .in_14(_14), .in_15(_15),
    .out(B));

  // Other names for the same wires on the sheet: a_t[3:0] = a_2; b_t[3:0] = b_2; czin[3:0] = c_2
endmodule
