// Digital circuit Registrador32bit.dig as structural Verilog
module Registrador32bit (
  input  Enable,
  input  Clk,
  input  [3:0] c,
  input  [3:0] a_2,
  input  [3:0] b_2,
  input  [31:0] C_2,
  output [31:0] A,
  output [31:0] B
);

  wire and_1_out, demultiplexer_1_out_0, demultiplexer_1_out_1, demultiplexer_1_out_2, demultiplexer_1_out_3,
       demultiplexer_1_out_4, demultiplexer_1_out_5, demultiplexer_1_out_6, demultiplexer_1_out_7,
       demultiplexer_1_out_8, demultiplexer_1_out_9, demultiplexer_1_out_10, demultiplexer_1_out_11,
       demultiplexer_1_out_12, demultiplexer_1_out_13, demultiplexer_1_out_14, demultiplexer_1_out_15;
  wire [31:0] _0, _1, _2, _3, _4, _5, _6, _7, _8, _9, _10, _11, _12, _13, _14, _15;
  wire [31:1] undriven;

  and and_1 (and_1_out, Enable, Clk);
  Demultiplexer #(.Selector_Bits(4)) demultiplexer_1 (
    .sel(c), .in(and_1_out), .out_0(demultiplexer_1_out_0), .out_1(demultiplexer_1_out_1),
    .out_2(demultiplexer_1_out_2), .out_3(demultiplexer_1_out_3), .out_4(demultiplexer_1_out_4),
    .out_5(demultiplexer_1_out_5), .out_6(demultiplexer_1_out_6), .out_7(demultiplexer_1_out_7),
    .out_8(demultiplexer_1_out_8), .out_9(demultiplexer_1_out_9), .out_10(demultiplexer_1_out_10),
    .out_11(demultiplexer_1_out_11), .out_12(demultiplexer_1_out_12), .out_13(demultiplexer_1_out_13),
    .out_14(demultiplexer_1_out_14), .out_15(demultiplexer_1_out_15));
  D_FF #(.Bits(32)) u__0 (.D({undriven, 1'b0}), .C(demultiplexer_1_out_0), .Q(_0));  // open: nQ
  D_FF #(.Bits(32)) u__1 (.D(C_2), .C(demultiplexer_1_out_1), .Q(_1));  // open: nQ
  D_FF #(.Bits(32)) u__2 (.D(C_2), .C(demultiplexer_1_out_2), .Q(_2));  // open: nQ
  D_FF #(.Bits(32)) u__3 (.D(C_2), .C(demultiplexer_1_out_3), .Q(_3));  // open: nQ
  D_FF #(.Bits(32)) u__4 (.D(C_2), .C(demultiplexer_1_out_4), .Q(_4));  // open: nQ
  D_FF #(.Bits(32)) u__5 (.D(C_2), .C(demultiplexer_1_out_5), .Q(_5));  // open: nQ
  D_FF #(.Bits(32)) u__6 (.D(C_2), .C(demultiplexer_1_out_6), .Q(_6));  // open: nQ
  D_FF #(.Bits(32)) u__7 (.D(C_2), .C(demultiplexer_1_out_7), .Q(_7));  // open: nQ
  D_FF #(.Bits(32)) u__8 (.D(C_2), .C(demultiplexer_1_out_8), .Q(_8));  // open: nQ
  D_FF #(.Bits(32)) u__9 (.D(C_2), .C(demultiplexer_1_out_9), .Q(_9));  // open: nQ
  D_FF #(.Bits(32)) u__10 (.D(C_2), .C(demultiplexer_1_out_10), .Q(_10));  // open: nQ
  D_FF #(.Bits(32)) u__11 (.D(C_2), .C(demultiplexer_1_out_11), .Q(_11));  // open: nQ
  D_FF #(.Bits(32)) u__12 (.D(C_2), .C(demultiplexer_1_out_12), .Q(_12));  // open: nQ
  D_FF #(.Bits(32)) u__13 (.D(C_2), .C(demultiplexer_1_out_13), .Q(_13));  // open: nQ
  D_FF #(.Bits(32)) u__14 (.D(C_2), .C(demultiplexer_1_out_14), .Q(_14));  // open: nQ
  D_FF #(.Bits(32)) u__15 (.D(C_2), .C(demultiplexer_1_out_15), .Q(_15));  // open: nQ
  Multiplexer #(.Selector_Bits(4), .Bits(32)) multiplexer_1 (
    .sel(a_2), .in_0(_0), .in_1(_1), .in_2(_2), .in_3(_3), .in_4(_4), .in_5(_5), .in_6(_6), .in_7(_7),
    .in_8(_8), .in_9(_9), .in_10(_10), .in_11(_11), .in_12(_12), .in_13(_13), .in_14(_14), .in_15(_15),
    .out(A));
  Multiplexer #(.Selector_Bits(4), .Bits(32)) multiplexer_2 (
    .sel(b_2), .in_0(_0), .in_1(_1), .in_2(_2), .in_3(_3), .in_4(_4), .in_5(_5), .in_6(_6), .in_7(_7),
    .in_8(_8), .in_9(_9), .in_10(_10), .in_11(_11), .in_12(_12), .in_13(_13), .in_14(_14), .in_15(_15),
    .out(B));
  // Pins of 1 and 32 bits meet at {undriven, 1'b0}
  // Pins of 1 and 32 bits meet at C_2
  // Pins of 1 and 4 bits meet at c
  // Pins of 1 and 4 bits meet at b_2
  // Pins of 1 and 32 bits meet at B
  // Pins of 1 and 4 bits meet at a_2
  // Pins of 1 and 32 bits meet at A

  // Other names for the same wires on the sheet: a_t[3:0] = a_2; b_t[3:0] = b_2; C_t[31:0] = C_2
endmodule
