// Digital circuit ULA.dig as structural Verilog
module ULA (
  input  [31:0] Alpha,
  input  [31:0] Beta,
  input  [3:0] fun,
  output Gamma
);

  Multiplexer #(.Selector_Bits(4), .Bits(32)) multiplexer_1 (.sel(fun));  // open: in_0, in_1, in_2, in_3, in_4, in_5, in_6, in_7, in_8, in_9, in_10, in_11, in_12, in_13, in_14, in_15, out
endmodule
