// Digital circuit Desloca_2x.dig as structural Verilog
module Desloca_2x (
  input  [31:0] A,
  input  sh,
  output [31:0] S
);

  wire [31:0] deslocador_32_left_1_s;

  Deslocador_32_left deslocador_32_left_1 (.A(A), .sh(sh), .S(deslocador_32_left_1_s));
  Deslocador_32_left deslocador_32_left_2 (.A(deslocador_32_left_1_s), .sh(sh), .S(S));
endmodule
