// Digital circuit Deslocador_32_left.dig as structural Verilog
module Deslocador_32_left (
  input  [31:0] A,
  input  sh,
  output [31:0] S
);

  wire deslocador_4bit_inicio_1_p4, deslocador_4bit_meio_1_p5, deslocador_4bit_meio_2_out,
       deslocador_4bit_meio_3_out, deslocador_4bit_meio_4_out, deslocador_4bit_meio_5_out,
       deslocador_4bit_meio_6_out;

  // Deslocador_4bit_Inicio deslocador_4bit_inicio_1: pin names not known; wires that end beside it: A[3:0], sh, S[3:0], deslocador_4bit_inicio_1_p4
  // Deslocador_4bit_meio deslocador_4bit_meio_1: pin names not known; wires that end beside it: A[7:4], sh, deslocador_4bit_inicio_1_p4, S[7:4], deslocador_4bit_meio_1_p5
  Deslocador_4bit_meio deslocador_4bit_meio_2 (
    .A(A[11:8]), .sh(sh), .in(deslocador_4bit_meio_1_p5), .S(S[11:8]), .out(deslocador_4bit_meio_2_out));
  Deslocador_4bit_meio deslocador_4bit_meio_3 (
    .A(A[15:12]), .sh(sh), .in(deslocador_4bit_meio_2_out), .S(S[15:12]), .out(deslocador_4bit_meio_3_out));
  Deslocador_4bit_meio deslocador_4bit_meio_4 (
    .A(A[19:16]), .sh(sh), .in(deslocador_4bit_meio_3_out), .S(S[19:16]), .out(deslocador_4bit_meio_4_out));
  Deslocador_4bit_meio deslocador_4bit_meio_5 (
    .A(A[23:20]), .sh(sh), .in(deslocador_4bit_meio_4_out), .S(S[23:20]), .out(deslocador_4bit_meio_5_out));
  Deslocador_4bit_meio deslocador_4bit_meio_6 (
    .A(A[27:24]), .sh(sh), .in(deslocador_4bit_meio_5_out), .S(S[27:24]), .out(deslocador_4bit_meio_6_out));
  Deslocador_4bit_fim deslocador_4bit_fim_1 (.A(A[31:28]), .sh(sh), .in(deslocador_4bit_meio_6_out), .S(S[31:28]));
endmodule
