// Digital circuit Deslocador_4bit.dig as structural Verilog
module Deslocador_4bit (
  input  [3:0] A,
  input  sh,
  output [3:0] S
);

  wire multiplexer_1_out, multiplexer_2_out, multiplexer_3_out, multiplexer_4_out, undriven, undriven_2,
       undriven_3, undriven_4, undriven_5;

  Multiplexer multiplexer_1 (.sel(sh), .in_0(undriven), .in_1(undriven_2), .out(multiplexer_1_out));
  Multiplexer multiplexer_2 (.sel(sh), .in_0(undriven_2), .in_1(undriven_3), .out(multiplexer_2_out));
  Multiplexer multiplexer_3 (.sel(sh), .in_0(undriven_3), .in_1(undriven_4), .out(multiplexer_3_out));
  Multiplexer multiplexer_4 (.sel(sh), .in_0(undriven_4), .in_1(undriven_5), .out(multiplexer_4_out));
endmodule
