// Digital circuit Deslocador_MAIN.dig as structural Verilog
module Deslocador_MAIN (
  input  [31:0] A,
  input  [31:0] B
);

  Deslocador_32_left deslocador_32_left_1 (.A(A), .sh(B[0]));  // open: S
endmodule
