// Digital circuit Desloca_16x.dig as structural Verilog
module Desloca_16x (
  input  [31:0] A,
  input  sh,
  output [31:0] S
);

  wire [31:0] desloca_8x_1_s;

  Desloca_8x desloca_8x_1 (.A(A), .sh(sh), .S(desloca_8x_1_s));
  Desloca_8x desloca_8x_2 (.A(desloca_8x_1_s), .sh(sh), .S(S));
endmodule
