// Digital circuit Desloca_32x.dig as structural Verilog
module Desloca_32x (
  input  [31:0] A,
  input  sh,
  output [31:0] S
);

  wire [31:0] desloca_16x_1_s;

  Desloca_16x desloca_16x_1 (.A(A), .sh(sh), .S(desloca_16x_1_s));
  Desloca_16x desloca_16x_2 (.A(desloca_16x_1_s), .sh(sh), .S(S));
endmodule
