// Digital circuit Desloca_4x.dig as structural Verilog
module Desloca_4x (
  input  [31:0] A,
  input  sh,
  output [31:0] S
);

  wire [31:0] desloca_2x_1_s;

  Desloca_2x desloca_2x_1 (.A(A), .sh(sh), .S(desloca_2x_1_s));
  Desloca_2x desloca_2x_2 (.A(desloca_2x_1_s), .sh(sh), .S(S));
endmodule
