// Digital circuit Desloca_8x.dig as structural Verilog
module Desloca_8x (
  input  [31:0] A,
  input  sh,
  output [31:0] S
);

  wire [31:0] desloca_4x_1_s;

  Desloca_4x desloca_4x_1 (.A(A), .sh(sh), .S(desloca_4x_1_s));
  Desloca_4x desloca_4x_2 (.A(desloca_4x_1_s), .sh(sh), .S(S));
endmodule
