// Digital circuit Deslocador_32_left.dig as structural Verilog
module Deslocador_32_left (
  input  [31:0] A,
  input  sh,
  output [31:0] S
);

  wire deslocador_4bit_1_out, deslocador_4bit_2_out, deslocador_4bit_3_out, deslocador_4bit_4_out,
       deslocador_4bit_5_out, deslocador_4bit_6_out, deslocador_4bit_7_out, deslocador_4bit_8_out;

  Deslocador_4bit deslocador_4bit_1 (.A(A[3:0]), .sh(sh), .in(1'b0), .S(S[3:0]), .out(deslocador_4bit_1_out));
  Deslocador_4bit deslocador_4bit_2 (
    .A(A[7:4]), .sh(sh), .in(deslocador_4bit_1_out), .S(S[7:4]), .out(deslocador_4bit_2_out));
  Deslocador_4bit deslocador_4bit_3 (
    .A(A[11:8]), .sh(sh), .in(deslocador_4bit_2_out), .S(S[11:8]), .out(deslocador_4bit_3_out));
  Deslocador_4bit deslocador_4bit_4 (
    .A(A[15:12]), .sh(sh), .in(deslocador_4bit_3_out), .S(S[15:12]), .out(deslocador_4bit_4_out));
  Deslocador_4bit deslocador_4bit_5 (
    .A(A[19:16]), .sh(sh), .in(deslocador_4bit_4_out), .S(S[19:16]), .out(deslocador_4bit_5_out));
  Deslocador_4bit deslocador_4bit_6 (
    .A(A[23:20]), .sh(sh), .in(deslocador_4bit_5_out), .S(S[23:20]), .out(deslocador_4bit_6_out));
  Deslocador_4bit deslocador_4bit_7 (
    .A(A[27:24]), .sh(sh), .in(deslocador_4bit_6_out), .S(S[27:24]), .out(deslocador_4bit_7_out));
  Deslocador_4bit deslocador_4bit_8 (
    .A(A[31:28]), .sh(sh), .in(deslocador_4bit_7_out), .S(S[31:28]), .out(deslocador_4bit_8_out));
  // also tied to GND on the sheet: deslocador_4bit_8_out
endmodule
