// Digital circuit Deslocador_4bit_meio.dig as structural Verilog
module Deslocador_4bit_meio (
  input  [3:0] A,
  input  sh,
  input  [3:0] in,
  output [3:0] S,
  output [3:0] out
);

  Multiplexer multiplexer_1 (.sel(sh), .in_0(in[0]), .in_1(A[0]), .out(S[0]));
  Multiplexer multiplexer_2 (.sel(sh), .in_0(A[0]), .in_1(A[1]), .out(S[1]));
  Multiplexer multiplexer_3 (.sel(sh), .in_0(A[1]), .in_1(A[2]), .out(S[2]));
  Multiplexer multiplexer_4 (.sel(sh), .in_0(A[2]), .in_1(A[3]), .out(S[3]));
  // Pins of 1 and 4 bits meet at in
  // Pins of 1 and 4 bits meet at {out[3:1], A[3]}

  assign out[0] = A[3];
endmodule
