// Digital circuit Deslocador_MAIN.dig as structural Verilog
module Deslocador_MAIN (
  input  [31:0] A,
  input  [31:0] B,
  output [31:0] S
);

  wire [31:0] desloca_2x_1_s, desloca_4x_1_s, desloca_8x_1_s, desloca_16x_1_s, deslocador_32_left_1_s;

  Deslocador_32_left deslocador_32_left_1 (.A(A), .sh(B[0]), .S(deslocador_32_left_1_s));
  Desloca_2x desloca_2x_1 (.A(deslocador_32_left_1_s), .sh(B[1]), .S(desloca_2x_1_s));
  Desloca_4x desloca_4x_1 (.A(desloca_2x_1_s), .sh(B[2]), .S(desloca_4x_1_s));
  Desloca_8x desloca_8x_1 (.A(desloca_4x_1_s), .sh(B[3]), .S(desloca_8x_1_s));
  Desloca_16x desloca_16x_1 (.A(desloca_8x_1_s), .sh(B[4]), .S(desloca_16x_1_s));
  Desloca_32x desloca_32x_1 (.A(desloca_16x_1_s), .sh(B[5]), .S(S));
endmodule
