// Digital circuit Desloca_16xR.dig as structural Verilog
module Desloca_16xR (
  input  [31:0] A,
  input  sh,
  output [31:0] S
);

  wire [31:0] desloca_8xr_1_s;

  Desloca_8xR desloca_8xr_1 (.A(A), .sh(sh), .S(desloca_8xr_1_s));
  Desloca_8xR desloca_8xr_2 (.A(desloca_8xr_1_s), .sh(sh), .S(S));
endmodule
