// Digital circuit Desloca_2xR.dig as structural Verilog
module Desloca_2xR (
  input  [31:0] A,
  input  sh,
  output [31:0] S
);

  wire [31:0] deslocador_32bit_right_1_s;

  Deslocador_32bit_right deslocador_32bit_right_1 (.A(A), .sh(sh), .S(deslocador_32bit_right_1_s));
  Deslocador_32bit_right deslocador_32bit_right_2 (.A(deslocador_32bit_right_1_s), .sh(sh), .S(S));
endmodule
