// Digital circuit Desloca_32xR.dig as structural Verilog
module Desloca_32xR (
  input  [31:0] A,
  input  sh,
  output [31:0] S
);

  wire [31:0] desloca_16xr_1_s;

  Desloca_16xR desloca_16xr_1 (.A(A), .sh(sh), .S(desloca_16xr_1_s));
  Desloca_16xR desloca_16xr_2 (.A(desloca_16xr_1_s), .sh(sh), .S(S));
endmodule
