// Digital circuit Desloca_4xR.dig as structural Verilog
module Desloca_4xR (
  input  [31:0] A,
  input  sh,
  output [31:0] S
);

  wire [31:0] desloca_2xr_1_s;

  Desloca_2xR desloca_2xr_1 (.A(A), .sh(sh), .S(desloca_2xr_1_s));
  Desloca_2xR desloca_2xr_2 (.A(desloca_2xr_1_s), .sh(sh), .S(S));
endmodule
