// Digital circuit Desloca_8xR.dig as structural Verilog
module Desloca_8xR (
  input  [31:0] A,
  input  sh,
  output [31:0] S
);

  wire [31:0] desloca_4xr_1_s;

  Desloca_4xR desloca_4xr_1 (.A(A), .sh(sh), .S(desloca_4xr_1_s));
  Desloca_4xR desloca_4xr_2 (.A(desloca_4xr_1_s), .sh(sh), .S(S));
endmodule
