// Digital circuit Deslocador_32bit_right.dig as structural Verilog
module Deslocador_32bit_right (
  input  [31:0] A,
  input  sh,
  output [31:0] S
);

  wire _4bit_deslocador_2_out, _4bit_deslocador_3_out, _4bit_deslocador_4_out, _4bit_deslocador_5_out,
       _4bit_deslocador_6_out, _4bit_deslocador_7_out, _4bit_deslocador_8_out;

  _4bit_deslocador _4bit_deslocador_1 (.A(A[3:0]), .sh(sh), .in(_4bit_deslocador_2_out), .S(S[3:0]));  // open: out
  _4bit_deslocador _4bit_deslocador_2 (
    .A(A[7:4]), .sh(sh), .in(_4bit_deslocador_3_out), .S(S[7:4]), .out(_4bit_deslocador_2_out));
  _4bit_deslocador _4bit_deslocador_3 (
    .A(A[11:8]), .sh(sh), .in(_4bit_deslocador_4_out), .S(S[11:8]), .out(_4bit_deslocador_3_out));
  _4bit_deslocador _4bit_deslocador_4 (
    .A(A[15:12]), .sh(sh), .in(_4bit_deslocador_5_out), .S(S[15:12]), .out(_4bit_deslocador_4_out));
  _4bit_deslocador _4bit_deslocador_5 (
    .A(A[19:16]), .sh(sh), .in(_4bit_deslocador_6_out), .S(S[19:16]), .out(_4bit_deslocador_5_out));
  _4bit_deslocador _4bit_deslocador_6 (
    .A(A[23:20]), .sh(sh), .in(_4bit_deslocador_7_out), .S(S[23:20]), .out(_4bit_deslocador_6_out));
  _4bit_deslocador _4bit_deslocador_7 (
    .A(A[27:24]), .sh(sh), .in(_4bit_deslocador_8_out), .S(S[27:24]), .out(_4bit_deslocador_7_out));
  _4bit_deslocador _4bit_deslocador_8 (.A(A[31:28]), .sh(sh), .in(1'b0), .S(S[31:28]), .out(_4bit_deslocador_8_out));
endmodule
