// Digital circuit Deslocador_right_main.dig as structural Verilog
module Deslocador_right_main (
  input  [31:0] A,
  input  [31:0] B,
  output [31:0] S
);

  wire [31:0] desloca_2xr_1_s, desloca_4xr_1_s, desloca_8xr_1_s, desloca_16xr_1_s, deslocador_32bit_right_1_s;

  Deslocador_32bit_right deslocador_32bit_right_1 (.A(A), .sh(B[0]), .S(deslocador_32bit_right_1_s));
  Desloca_2xR desloca_2xr_1 (.A(deslocador_32bit_right_1_s), .sh(B[1]), .S(desloca_2xr_1_s));
  Desloca_4xR desloca_4xr_1 (.A(desloca_2xr_1_s), .sh(B[2]), .S(desloca_4xr_1_s));
  Desloca_8xR desloca_8xr_1 (.A(desloca_4xr_1_s), .sh(B[3]), .S(desloca_8xr_1_s));
  Desloca_16xR desloca_16xr_1 (.A(desloca_8xr_1_s), .sh(B[4]), .S(desloca_16xr_1_s));
  Desloca_32xR desloca_32xr_1 (.A(desloca_16xr_1_s), .sh(B[5]), .S(S));
endmodule
