// Digital circuit Carry_LA.dig as structural Verilog
module Carry_LA (
  input  Cin,
  input  [3:0] A,
  input  [3:0] B,
  output [3:0] S,
  output Co
);

  wire and_1_out, and_2_out, and_3_out, and_4_out, and_5_out, and_6_out, and_7_out, and_8_out, and_9_out,
       and_10_out, or_2_out, or_3_out, or_4_out, somador_g_p_1_g, somador_g_p_1_p, somador_g_p_2_g,
       somador_g_p_2_p, somador_g_p_3_g, somador_g_p_3_p, somador_g_p_4_g, somador_g_p_4_p;

  and and_1 (and_1_out, Cin, somador_g_p_1_p, somador_g_p_2_p, somador_g_p_3_p, somador_g_p_4_p);
  Somador_G_P somador_g_p_1 (.B(B[3]), .A(A[3]), .G(somador_g_p_1_g), .P(somador_g_p_1_p));
  and and_2 (and_2_out, somador_g_p_1_p, somador_g_p_2_p, somador_g_p_3_p, somador_g_p_4_g);
  and and_3 (and_3_out, somador_g_p_1_p, somador_g_p_2_p, somador_g_p_3_g);
  or or_1 (Co, somador_g_p_1_g, and_4_out, and_3_out, and_2_out, and_1_out);
  and and_4 (and_4_out, somador_g_p_1_p, somador_g_p_2_g);
  and and_5 (and_5_out, Cin, somador_g_p_2_p, somador_g_p_3_p, somador_g_p_4_p);
  Somador_G_P somador_g_p_2 (.B(B[2]), .A(A[2]), .G(somador_g_p_2_g), .P(somador_g_p_2_p));
  and and_6 (and_6_out, somador_g_p_2_p, somador_g_p_3_p, somador_g_p_4_g);
  or or_2 (or_2_out, somador_g_p_2_g, and_7_out, and_6_out, and_5_out);
  and and_7 (and_7_out, somador_g_p_2_p, somador_g_p_3_g);
  xor xor_1 (S[3], somador_g_p_1_p, somador_g_p_1_g, or_2_out);
  and and_8 (and_8_out, Cin, somador_g_p_3_p, somador_g_p_4_p);
  or or_3 (or_3_out, somador_g_p_3_g, and_9_out, and_8_out);
  and and_9 (and_9_out, somador_g_p_3_p, somador_g_p_4_g);
  xor xor_2 (S[2], somador_g_p_2_p, somador_g_p_2_g, or_3_out);
  Somador_G_P somador_g_p_3 (.B(B[1]), .A(A[1]), .G(somador_g_p_3_g), .P(somador_g_p_3_p));
  and and_10 (and_10_out, Cin, somador_g_p_4_p);
  or or_4 (or_4_out, somador_g_p_4_g, and_10_out);
  xor xor_3 (S[1], somador_g_p_3_p, somador_g_p_3_g, or_4_out);
  xor xor_4 (S[0], somador_g_p_4_g, somador_g_p_4_p, Cin);
  Somador_G_P somador_g_p_4 (.B(B[0]), .A(A[0]), .G(somador_g_p_4_g), .P(somador_g_p_4_p));

  // Other names for the same wires on the sheet: Cout = Co
endmodule
