// Digital circuit Carry_LA_novo.dig as structural Verilog
module Carry_LA_novo (
  input  Cin,
  input  [3:0] B,
  input  [3:0] A,
  output [3:0] S,
  output Cout
);

  wire not_1_out;

  not not_1 (not_1_out, Cin);
  // Not not_2 has open pins: in=not_1_out, out=open
  // And and_1 is placed but not wired
  // AB_nor_nand ab_nor_nand_1: pin names not known; wires that end beside it: A[0], B[0]
  // And and_2 has open pins: In_1=open, In_2=not_1_out, out=open
  // And and_3 is placed but not wired
  // AB_nor_nand ab_nor_nand_2: pin names not known; wires that end beside it: A[1], B[1]
  // And and_4 has open pins: In_1=open, In_2=open, In_3=not_1_out, out=open
  // And and_5 is placed but not wired
  // AB_nor_nand ab_nor_nand_3: pin names not known; wires that end beside it: A[2], B[2]
  // And and_6 is placed but not wired
  // And and_7 has open pins: In_1=open, In_2=open, In_3=open, In_4=not_1_out, out=open
  // AB_nor_nand ab_nor_nand_4: pin names not known; wires that end beside it: A[3], B[3]
  // And and_8 is placed but not wired
  // And and_9 is placed but not wired
  // And and_10 is placed but not wired
  // And and_11 has open pins: In_1=open, In_2=open, In_3=open, In_4=not_1_out, out=open
  // And and_12 is placed but not wired
  // And and_13 is placed but not wired
  // And and_14 is placed but not wired

  // Notes on the sheet:
  //   https://www.elprocus.com/carry-look-ahead-adder/
endmodule
