// Digital circuit Somador_32bit.dig as structural Verilog
module Somador_32bit (
  input  [31:0] A,
  input  [31:0] B,
  output [31:0] S
);

  wire carry_la_1_cout, carry_la_3_cout, carry_la_4_cout, carry_la_5_cout, carry_la_6_cout, carry_la_7_cout;

  Carry_LA carry_la_1 (.Cin(1'b0), .A(A[3:0]), .B(B[3:0]), .S(S[3:0]), .Cout(carry_la_1_cout));
  Carry_LA carry_la_2 (.Cin(carry_la_1_cout), .A(A[7:4]), .B(B[7:4]), .S(S[7:4]));  // open: Cout
  Carry_LA carry_la_3 (.A(A[11:8]), .B(B[11:8]), .S(S[11:8]), .Cout(carry_la_3_cout));  // open: Cin
  Carry_LA carry_la_4 (.Cin(carry_la_3_cout), .A(A[15:12]), .B(B[15:12]), .S(S[15:12]), .Cout(carry_la_4_cout));
  Carry_LA carry_la_5 (.Cin(carry_la_4_cout), .A(A[19:16]), .B(B[19:16]), .S(S[19:16]), .Cout(carry_la_5_cout));
  Carry_LA carry_la_6 (.Cin(carry_la_5_cout), .A(A[23:20]), .B(B[23:20]), .S(S[23:20]), .Cout(carry_la_6_cout));
  Carry_LA carry_la_7 (.Cin(carry_la_6_cout), .A(A[27:24]), .B(B[27:24]), .S(S[27:24]), .Cout(carry_la_7_cout));
  Carry_LA carry_la_8 (.Cin(carry_la_7_cout), .A(A[31:28]), .B(B[31:28]), .S(S[31:28]));  // open: Cout
endmodule
