// Digital circuit Subtrator_32Bit.dig as structural Verilog
module Subtrator_32Bit (
  input  [31:0] A,
  input  [31:0] B,
  output [31:0] S
);

  wire [31:0] not_1_out, somador_32bit_1_s;

  assign not_1_out = ~B;  // Not not_1, 32 bits wide
  Somador_32bit somador_32bit_1 (.A(A), .B(not_1_out), .S(somador_32bit_1_s));
  // Somador_32bit somador_32bit_2: pin names not known; wires that end beside it: somador_32bit_1_s, 1'b1, S
endmodule
