// Digital circuit ULA.dig as structural Verilog
module ULA (
  input  [31:0] Alpha,
  input  [31:0] Beta,
  input  [2:0] fun,
  output [31:0] Gamma
);

  wire [31:0] and_1_out, deslocador_right_main_1_s, Left_s, not_1_out, or_1_out, somador_32bit_1_s,
       subtrator_32bit_1_s, xor_1_out;

  Somador_32bit somador_32bit_1 (.A(Alpha), .B(Beta), .S(somador_32bit_1_s));
  Subtrator_32Bit subtrator_32bit_1 (.A(Alpha), .B(Beta), .S(subtrator_32bit_1_s));
  assign and_1_out = Alpha & Beta;  // And and_1, 32 bits wide
  assign or_1_out = Alpha | Beta;  // Or or_1, 32 bits wide
  assign xor_1_out = Alpha ^ Beta;  // XOr xor_1, 32 bits wide
  assign not_1_out = ~Alpha;  // Not not_1, 32 bits wide
  Deslocador_MAIN Left (.A(Alpha), .B(Beta), .S(Left_s));
  Deslocador_right_main deslocador_right_main_1 (.A(Alpha), .B(Beta), .S(deslocador_right_main_1_s));
  Multiplexer #(.Selector_Bits(3), .Bits(32)) multiplexer_1 (
    .sel(fun), .in_0(somador_32bit_1_s), .in_1(subtrator_32bit_1_s), .in_2(and_1_out), .in_3(or_1_out),
    .in_4(xor_1_out), .in_5(not_1_out), .in_6(Left_s), .in_7(deslocador_right_main_1_s), .out(Gamma));

  // Other names for the same wires on the sheet: A[31:0] = Alpha; B[31:0] = Beta
endmodule
