// Digital circuit ip.dig as structural Verilog
module ip (
  input  [23:0] A,
  input  [23:0] B,
  output [23:0] S
);

  wire carry_la_1_co, carry_la_2_co, carry_la_3_co, carry_la_4_co, carry_la_5_co;

  Carry_LA carry_la_1 (.Cin(1'b0), .A(A[3:0]), .B(B[3:0]), .S(S[3:0]), .Co(carry_la_1_co));
  Carry_LA carry_la_2 (.Cin(carry_la_1_co), .A(A[7:4]), .B(B[7:4]), .S(S[7:4]), .Co(carry_la_2_co));
  Carry_LA carry_la_3 (.Cin(carry_la_2_co), .A(A[11:8]), .B(B[11:8]), .S(S[11:8]), .Co(carry_la_3_co));
  Carry_LA carry_la_4 (.Cin(carry_la_3_co), .A(A[15:12]), .B(B[15:12]), .S(S[15:12]), .Co(carry_la_4_co));
  Carry_LA carry_la_5 (.Cin(carry_la_4_co), .A(A[19:16]), .B(B[19:16]), .S(S[19:16]), .Co(carry_la_5_co));
  Carry_LA carry_la_6 (.Cin(carry_la_5_co), .A(A[23:20]), .B(B[23:20]), .S(S[23:20]));  // open: Co

  // Other names for the same wires on the sheet: a0[3:0] = A[3:0]; a1[3:0] = A[7:4]; a2[3:0] = A[11:8];
  //   a3[3:0] = A[15:12]; a4[3:0] = A[19:16]; a5[3:0] = A[23:20]; b0[3:0] = B[3:0]; b1[3:0] = B[7:4];
  //   b2[3:0] = B[11:8]; b3[3:0] = B[15:12]; b4[3:0] = B[19:16]; b5[3:0] = B[23:20]
endmodule
