// Digital circuit registradores.dig as structural Verilog
module registradores (
  input  C,
  input  clk,
  input  [3:0] a,
  input  [3:0] b,
  input  [3:0] c_2,
  input  wenable,
  output [31:0] Saida_B,
  output [31:0] Saida_A,
  output [31:0] Saida_C
);

  wire [31:0] register_1_q, register_2_q, register_3_q, register_4_q, register_5_q, register_6_q,
       register_7_q, register_8_q, register_9_q, register_10_q, register_11_q, register_12_q, register_13_q,
       register_14_q, register_15_q, register_16_q;

  Register register_1 (.D(C), .C(clk), .en(clk), .Q(register_1_q[0]));
  Register register_2 (.D(C), .C(clk), .en(clk), .Q(register_2_q[0]));
  Register register_3 (.D(C), .C(clk), .en(clk), .Q(register_3_q[0]));
  Register register_4 (.D(C), .C(clk), .en(clk), .Q(register_4_q[0]));
  Register register_5 (.D(C), .C(clk), .en(clk), .Q(register_5_q[0]));
  Register register_6 (.D(C), .C(clk), .en(clk), .Q(register_6_q[0]));
  Register register_7 (.D(C), .C(clk), .en(clk), .Q(register_7_q[0]));
  Register register_8 (.D(C), .C(clk), .en(clk), .Q(register_8_q[0]));
  Register register_9 (.D(C), .C(clk), .en(clk), .Q(register_9_q[0]));
  Register register_10 (.D(C), .C(clk), .en(clk), .Q(register_10_q[0]));
  Register register_11 (.D(C), .C(clk), .en(clk), .Q(register_11_q[0]));
  Register register_12 (.D(C), .C(clk), .en(clk), .Q(register_12_q[0]));
  Register register_13 (.D(C), .C(clk), .en(clk), .Q(register_13_q[0]));
  Register register_14 (.D(C), .C(clk), .en(clk), .Q(register_14_q[0]));
  Register register_15 (.D(C), .C(clk), .en(clk), .Q(register_15_q[0]));
  Register register_16 (.D(C), .C(clk), .en(clk), .Q(register_16_q[0]));
  Multiplexer #(.Selector_Bits(4), .Bits(32)) multiplexer_1 (
    .sel(a), .in_0(register_1_q), .in_8(register_9_q), .out(Saida_A));  // open: in_1, in_2, in_3, in_4, in_5, in_6, in_7, in_9, in_10, in_11, in_12, in_13, in_14, in_15
  Multiplexer #(.Selector_Bits(4), .Bits(32)) multiplexer_2 (
    .sel(b), .in_8(register_9_q), .out(Saida_B));  // open: in_0, in_1, in_2, in_3, in_4, in_5, in_6, in_7, in_9, in_10, in_11, in_12, in_13, in_14, in_15
  Multiplexer #(.Selector_Bits(4), .Bits(32)) multiplexer_3 (
    .sel(c_2), .in_0(register_1_q), .in_1(register_2_q), .in_2(register_3_q), .in_3(register_4_q),
    .in_4(register_5_q), .in_5(register_6_q), .in_6(register_7_q), .in_7(register_8_q), .in_8(register_9_q),
    .in_9(register_10_q), .in_10(register_11_q), .in_11(register_12_q), .in_12(register_13_q),
    .in_13(register_14_q), .in_14(register_15_q), .in_15(register_16_q), .out(Saida_C));
  // Pins of 1 and 4 bits meet at a
  // Pins of 1 and 4 bits meet at b
  // Pins of 1 and 4 bits meet at c_2
  // Pins of 1 and 32 bits meet at register_9_q
  // Pins of 1 and 32 bits meet at register_10_q
  // Pins of 1 and 32 bits meet at register_11_q
  // Pins of 1 and 32 bits meet at register_12_q
  // Pins of 1 and 32 bits meet at register_13_q
  // Pins of 1 and 32 bits meet at register_14_q
  // Pins of 1 and 32 bits meet at register_15_q
  // Pins of 1 and 32 bits meet at register_16_q
  // Pins of 1 and 32 bits meet at register_5_q

  assign wenable = clk;

  // Other names for the same wires on the sheet: c_t[3:0] = c_2; we = clk
endmodule
